# Fritzing sketch connection_diagram_teensy3-6_rpi_zero (saved by Fritzing 0.9.3b)
breadboards: 1

parts:
  Teensy1 = Teensy 3.6 (Basic)
  MCU1 = Raspberry Pi Zero

nets:
  GND: Teensy1.GND, Teensy1.GND1, MCU1.pin_6, MCU1.pin_25
  N1: Teensy1.D0, MCU1.pin_8
  N2: Teensy1.D1, MCU1.pin_10
  N3: Teensy1.3V3, Teensy1.3V3_1
  N4: Teensy1.Vin, MCU1.pin_2, MCU1.pin_4

custom parts:
  Teensy 3.6 (Basic): The Teensy is a complete USB-based microcontoller development system, in a very small footprint, capable of implementing many types of projects. All programming is done via the USB port. No special programmer is needed, only a standard micro-USB cable and a PC or Macintosh with a USB port.
